// Digital circuit ALU.dig as structural Verilog
module ALU (
  input  [2:0] in_1,
  input  [7:0] in_2,
  input  [7:0] in_3
);

  wire Div, Mult_t, Nand_t, SD, SE, Soma, Sub, Xor_t;
  wire [7:0] LSB, MULT, NAND, not_1_out, R, Shift_D, Shift_E, Subt, Sum, XOR;

  Seven_Seg_Hex seven_seg_hex_1 (.d(in_2[7:4]), .dp(1'b0));
  LED led_1 (.in(in_2[7]));
  Somador_8bits somador_8bits_1 (.Ain(in_2), .Bin(in_3), .Enable(Soma), .Cin(1'b0), .Sum(Sum));  // open: Cout
  Seven_Seg_Hex seven_seg_hex_2 (.d(in_2[3:0]), .dp(1'b0));
  LED led_2 (.in(in_2[6]));
  LED led_3 (.in(in_2[5]));
  LED led_4 (.in(in_2[4]));
  LED led_5 (.in(in_2[3]));
  LED led_6 (.in(in_2[2]));
  LED led_7 (.in(in_2[1]));
  // Subtrator_8bits subtrator_8bits_1: pin names not known; wires that end beside it: 1'b0, in_2, in_3, Sub, Subt
  Seven_Seg_Hex seven_seg_hex_3 (.d(in_3[7:4]), .dp(1'b0));
  LED led_8 (.in(in_2[0]));
  Seven_Seg_Hex seven_seg_hex_4 (.d(in_3[3:0]), .dp(1'b0));
  LED led_9 (.in(in_3[7]));
  LED led_10 (.in(in_3[6]));
  Shift_Direita shift_direita_1 (.Enable(SD), .In(in_2), .SD(Shift_D));
  LED led_11 (.in(in_3[5]));
  LED led_12 (.in(in_3[4]));
  LED led_13 (.in(in_3[3]));
  LED led_14 (.in(in_3[2]));
  seletor seletor_1 (
    .IN(in_1), .Soma(Soma), .Subtracao(Sub), .Mult(Mult_t), .Div(Div), .Shift_Direita(SD),
    .Shift_Esquerda(SE), .NAND(Nand_t), .XOR(Xor_t));
  LED led_15 (.in(in_3[1]));
  LED led_16 (.in(in_3[0]));
  Shift_Esquerda shift_esquerda_1 (.In_8bits(in_3), .Enable(SE), .SE(Shift_E));
  LED led_17 (.in(not_1_out[7]));
  LED led_18 (.in(not_1_out[6]));
  LED led_19 (.in(not_1_out[5]));
  LED led_20 (.in(not_1_out[4]));
  XOR xor_1 (.A(in_2), .B(in_3), .Enable(Xor_t), .XOR(XOR));
  assign R = Sum ^ Subt ^ MULT ^ Shift_D ^ Shift_E ^ XOR ^ NAND;  // XOr xor_2, 8 bits wide
  LED led_21 (.in(not_1_out[3]));
  LED led_22 (.in(not_1_out[2]));
  assign not_1_out = ~R;  // Not not_1, 8 bits wide
  LED led_23 (.in(not_1_out[1]));
  LED led_24 (.in(not_1_out[0]));
  NAND nand_1 (.A(in_2), .B(in_3), .Enable(Nand_t), .NAND(NAND));
  Multiplicador_8bits multiplicador_8bits_1 (.B(in_2), .A(in_3), .Enable(Mult_t), .LSB(LSB), .MSB(MULT));

  // Other names for the same wires on the sheet: A[7:0] = in_2; B[7:0] = in_3

  // Notes on the sheet:
  //   Operacoes
  //   Hexa primeiro numero
  //   Binario primeiro numero
  //   Hexa segundo numero
  //   Binario segundo numero
  //   Seletor
  //   Binario resultado
endmodule
