// Digital circuit Multiplicador_4bits.dig as structural Verilog
module Multiplicador_4bits (
  input  [7:0] B,
  input  [7:0] A,
  input  Enable,
  output [7:0] Mult
);

  wire A0, A1, A2, A3, B0, B1, B2, B3;
  wire [2:0] and_10_out;
  wire [3:0] and_1_out, and_2_out, and_3_out, somador_4bits_1_p3, somador_4bits_2_p3;
  wire [7:4] enable_1_aout, enable_1_bout;

  enable enable_1 (
    .Ain(A), .Enable(Enable), .Bin(B), .Aout({enable_1_aout, A3, A2, A1, A0}),
    .Bout({enable_1_bout, B3, B2, B1, B0}));
  and and_1 (and_1_out[3], A3, B1);
  and and_2 (and_2_out[3], A3, B2);
  and and_3 (and_3_out[3], A3, B3);
  and and_4 (and_1_out[2], A2, B1);
  and and_5 (and_2_out[2], A2, B2);
  and and_6 (and_3_out[2], A2, B3);
  and and_7 (and_1_out[1], A1, B1);
  and and_8 (and_2_out[1], A1, B2);
  and and_9 (and_3_out[1], A1, B3);
  and and_10 (and_10_out[2], A3, B0);
  and and_11 (and_1_out[0], A0, B1);
  and and_12 (and_2_out[0], A0, B2);
  and and_13 (and_3_out[0], A0, B3);
  and and_14 (and_10_out[1], A2, B0);
  // somador_4bits somador_4bits_1: pin names not known; wires that end beside it: 1'b0, and_1_out, somador_4bits_1_p3[3], {1'b0, and_10_out}, {somador_4bits_1_p3[2:0], Mult[1]}
  // somador_4bits somador_4bits_2: pin names not known; wires that end beside it: 1'b0, and_2_out, somador_4bits_2_p3[3], somador_4bits_1_p3, {somador_4bits_2_p3[2:0], Mult[2]}
  // somador_4bits somador_4bits_3: pin names not known; wires that end beside it: 1'b0, and_3_out, Mult[7], somador_4bits_2_p3, Mult[6:3]
  and and_15 (and_10_out[0], A1, B0);
  and and_16 (Mult[0], A0, B0);
endmodule
