// Digital circuit Multiplicador_8bits.dig as structural Verilog
module Multiplicador_8bits (
  input  [7:0] B,
  input  [7:0] A,
  input  Enable,
  output [7:0] LSB,
  output [7:0] MSB
);

  wire A0, A1, A2, A3, A4, A5, A6, A7, B0, B1, B2, B3, B4, B5, B6, B7, Cout0, Cout1, Cout2, Cout3, Cout4,
       Cout5, Cout6, Cout7, Cout8, Cout9, Cout10, Cout11, Cout12, Cout13, Cout14, Cout15, Cout16, Cout17,
       Cout18, Cout19, Cout20, Cout21, Cout22, Cout23, Cout24, Cout25, Cout26, Cout27, Cout28, Cout29,
       Cout30, Cout31, Cout32, Cout33, Cout34, Cout35, Cout36, Cout37, Cout38, Cout39, Cout40, Cout41,
       Cout42, Cout43, Cout44, Cout45, Cout46, Cout47, Cout48, Cout49, Cout50, Cout51, Cout52, Cout53,
       Cout54, PP0, PP1, PP2, PP3, PP4, PP5, PP6, PP7, PP8, PP9, PP10, PP11, PP12, PP13, PP14, PP15, PP16,
       PP17, PP18, PP19, PP20, PP21, PP22, PP23, PP24, PP25, PP26, PP27, PP28, PP29, PP30, PP31, PP32, PP33,
       PP34, PP35, PP36, PP37, PP38, PP39, PP40, PP41, PP43, PP44, PP45, PP46, PP47, PP48, PP49, PP50, PP51,
       PP52, PP53, PP54, PP55, PP56, PP57, PP58, PP59, PP60, PP61, PP62, PP63, SP0, SP1, SP2, SP3, SP4, SP5,
       SP6, SP7, SP8, SP9, SP10, SP11, SP12, SP13, SP14, SP15, SP16, SP17, SP18, SP19, SP20, SP21, SP22,
       SP23, SP24, SP25, SP26, SP27, SP28, SP29, SP30, SP31, SP32, SP33, SP34, SP35, SP36, SP37, SP38, SP39,
       SP40, SP41;

  Somador_1bit somador_1bit_1 (.A(PP63), .B(Cout53), .Cin(Cout54), .Cout(MSB[6]), .Sum(MSB[7]));
  Somador_1bit somador_1bit_2 (.A(PP61), .B(Cout50), .Cin(Cout51), .Cout(SP41), .Sum(Cout53));
  Somador_1bit somador_1bit_3 (.A(SP41), .B(PP62), .Cin(Cout52), .Cout(MSB[5]), .Sum(Cout54));
  Somador_1bit somador_1bit_4 (.A(PP58), .B(Cout46), .Cin(Cout47), .Cout(SP39), .Sum(Cout50));
  Somador_1bit somador_1bit_5 (.A(SP39), .B(PP59), .Cin(Cout48), .Cout(SP40), .Sum(Cout51));
  Somador_1bit somador_1bit_6 (.A(SP40), .B(PP60), .Cin(Cout49), .Cout(MSB[4]), .Sum(Cout52));
  Somador_1bit somador_1bit_7 (.A(PP54), .B(Cout41), .Cin(Cout42), .Cout(SP36), .Sum(Cout46));
  Somador_1bit somador_1bit_8 (.A(SP36), .B(PP55), .Cin(Cout43), .Cout(SP37), .Sum(Cout47));
  Somador_1bit somador_1bit_9 (.A(SP37), .B(PP56), .Cin(Cout44), .Cout(SP38), .Sum(Cout48));
  Somador_1bit somador_1bit_10 (.A(SP38), .B(PP57), .Cin(Cout45), .Cout(MSB[3]), .Sum(Cout49));
  enable enable_1 (
    .Ain(A), .Enable(Enable), .Bin(B), .Aout({A7, A6, A5, A4, A3, A2, A1, A0}),
    .Bout({B7, B6, B5, B4, B3, B2, B1, B0}));
  Somador_1bit somador_1bit_11 (.A(PP49), .B(Cout35), .Cin(Cout36), .Cout(SP32), .Sum(Cout41));
  Somador_1bit somador_1bit_12 (.A(SP32), .B(PP50), .Cin(Cout37), .Cout(SP33), .Sum(Cout42));
  Somador_1bit somador_1bit_13 (.A(SP33), .B(PP51), .Cin(Cout38), .Cout(SP34), .Sum(Cout43));
  Somador_1bit somador_1bit_14 (.A(SP34), .B(PP52), .Cin(Cout39), .Cout(SP35), .Sum(Cout44));
  Somador_1bit somador_1bit_15 (.A(SP35), .B(PP53), .Cin(Cout40), .Cout(MSB[2]), .Sum(Cout45));
  Somador_1bit somador_1bit_16 (.A(PP43), .B(Cout28), .Cin(Cout29), .Cout(SP27), .Sum(Cout35));
  Somador_1bit somador_1bit_17 (.A(SP27), .B(PP44), .Cin(Cout30), .Cout(SP28), .Sum(Cout36));
  Somador_1bit somador_1bit_18 (.A(SP28), .B(PP45), .Cin(Cout31), .Cout(SP29), .Sum(Cout37));
  Somador_1bit somador_1bit_19 (.A(SP29), .B(PP46), .Cin(Cout32), .Cout(SP30), .Sum(Cout38));
  Somador_1bit somador_1bit_20 (.A(SP30), .B(PP47), .Cin(Cout33), .Cout(SP31), .Sum(Cout39));
  Somador_1bit somador_1bit_21 (.A(SP31), .B(PP48), .Cin(Cout34), .Cout(MSB[1]), .Sum(Cout40));
  Somador_1bit somador_1bit_22 (.A(PP35), .B(Cout21), .Cin(1'b0), .Cout(SP21), .Sum(Cout28));
  Somador_1bit somador_1bit_23 (.A(SP21), .B(PP36), .Cin(Cout22), .Cout(SP22), .Sum(Cout29));
  Somador_1bit somador_1bit_24 (.A(SP22), .B(PP37), .Cin(Cout23), .Cout(SP23), .Sum(Cout30));
  Somador_1bit somador_1bit_25 (.A(SP23), .B(PP38), .Cin(Cout24), .Cout(SP24), .Sum(Cout31));
  Somador_1bit somador_1bit_26 (.A(SP24), .B(PP39), .Cin(Cout25), .Cout(SP25), .Sum(Cout32));
  Somador_1bit somador_1bit_27 (.A(SP25), .B(PP40), .Cin(Cout26), .Cout(SP26), .Sum(Cout33));
  Somador_1bit somador_1bit_28 (.A(SP26), .B(PP41), .Cin(Cout27), .Cout(MSB[0]), .Sum(Cout34));
  Somador_1bit somador_1bit_29 (.A(PP27), .B(PP28), .Cin(Cout15), .Cout(SP15), .Sum(Cout21));
  Somador_1bit somador_1bit_30 (.A(SP15), .B(PP29), .Cin(Cout16), .Cout(SP16), .Sum(Cout22));
  Somador_1bit somador_1bit_31 (.A(SP16), .B(PP30), .Cin(Cout17), .Cout(SP17), .Sum(Cout23));
  Somador_1bit somador_1bit_32 (.A(SP17), .B(PP31), .Cin(Cout18), .Cout(SP18), .Sum(Cout24));
  Somador_1bit somador_1bit_33 (.A(SP18), .B(PP32), .Cin(Cout19), .Cout(SP19), .Sum(Cout25));
  Somador_1bit somador_1bit_34 (.A(SP19), .B(PP33), .Cin(Cout20), .Cout(SP20), .Sum(Cout26));
  Somador_1bit somador_1bit_35 (.A(SP20), .B(PP34), .Cin(1'b0), .Cout(LSB[7]), .Sum(Cout27));
  Somador_1bit somador_1bit_36 (.A(PP20), .B(PP21), .Cin(Cout10), .Cout(SP10), .Sum(Cout15));
  Somador_1bit somador_1bit_37 (.A(SP10), .B(PP22), .Cin(Cout11), .Cout(SP11), .Sum(Cout16));
  Somador_1bit somador_1bit_38 (.A(SP11), .B(PP23), .Cin(Cout12), .Cout(SP12), .Sum(Cout17));
  Somador_1bit somador_1bit_39 (.A(SP12), .B(PP24), .Cin(Cout13), .Cout(SP13), .Sum(Cout18));
  Somador_1bit somador_1bit_40 (.A(SP13), .B(PP25), .Cin(Cout14), .Cout(SP14), .Sum(Cout19));
  Somador_1bit somador_1bit_41 (.A(SP14), .B(PP26), .Cin(1'b0), .Cout(LSB[6]), .Sum(Cout20));
  Somador_1bit somador_1bit_42 (.A(PP14), .B(PP15), .Cin(Cout6), .Cout(SP6), .Sum(Cout10));
  Somador_1bit somador_1bit_43 (.A(SP6), .B(PP16), .Cin(Cout7), .Cout(SP7), .Sum(Cout11));
  Somador_1bit somador_1bit_44 (.A(SP7), .B(PP17), .Cin(Cout8), .Cout(SP8), .Sum(Cout12));
  Somador_1bit somador_1bit_45 (.A(SP8), .B(PP18), .Cin(Cout9), .Cout(SP9), .Sum(Cout13));
  Somador_1bit somador_1bit_46 (.A(SP9), .B(PP19), .Cin(1'b0), .Cout(LSB[5]), .Sum(Cout14));
  and and_1 (PP63, B7, A7);
  Somador_1bit somador_1bit_47 (.A(PP9), .B(PP10), .Cin(Cout3), .Cout(SP3), .Sum(Cout6));
  Somador_1bit somador_1bit_48 (.A(SP3), .B(PP11), .Cin(Cout4), .Cout(SP4), .Sum(Cout7));
  Somador_1bit somador_1bit_49 (.A(SP4), .B(PP12), .Cin(Cout5), .Cout(SP5), .Sum(Cout8));
  Somador_1bit somador_1bit_50 (.A(SP5), .B(PP13), .Cin(1'b0), .Cout(LSB[4]), .Sum(Cout9));
  and and_2 (PP61, B6, A7);
  and and_3 (PP62, B7, A6);
  Somador_1bit somador_1bit_51 (.A(PP5), .B(PP6), .Cin(Cout1), .Cout(SP1), .Sum(Cout3));
  Somador_1bit somador_1bit_52 (.A(SP1), .B(PP7), .Cin(Cout2), .Cout(SP2), .Sum(Cout4));
  Somador_1bit somador_1bit_53 (.A(SP2), .B(PP8), .Cin(1'b0), .Cout(LSB[3]), .Sum(Cout5));
  and and_4 (PP58, B5, A7);
  and and_5 (PP59, B6, A6);
  and and_6 (PP60, B7, A5);
  Somador_1bit somador_1bit_54 (.A(PP2), .B(PP3), .Cin(Cout0), .Cout(SP0), .Sum(Cout1));
  Somador_1bit somador_1bit_55 (.A(SP0), .B(PP4), .Cin(1'b0), .Cout(LSB[2]), .Sum(Cout2));
  and and_7 (PP54, B4, A7);
  and and_8 (PP55, B5, A6);
  and and_9 (PP56, B6, A5);
  and and_10 (PP57, B7, A4);
  and and_11 (PP49, B3, A7);
  and and_12 (PP50, B4, A6);
  and and_13 (PP51, B5, A5);
  and and_14 (PP52, B6, A4);
  and and_15 (PP53, B7, A3);
  Somador_1bit somador_1bit_56 (.A(PP0), .B(PP1), .Cin(1'b0), .Cout(LSB[1]), .Sum(Cout0));
  and and_16 (PP43, B2, A7);
  and and_17 (PP44, B3, A6);
  and and_18 (PP45, B4, A5);
  and and_19 (PP46, B5, A4);
  and and_20 (PP47, B6, A3);
  and and_21 (PP48, B7, A2);
  and and_22 (PP35, B1, A7);
  and and_23 (PP36, B2, A6);
  and and_24 (PP37, B3, A5);
  and and_25 (PP38, B4, A4);
  and and_26 (PP39, B5, A3);
  and and_27 (PP40, B6, A2);
  and and_28 (PP41, B7, A1);
  and and_29 (PP27, B0, A7);
  and and_30 (PP28, B1, A6);
  and and_31 (PP29, B2, A5);
  and and_32 (PP30, B3, A4);
  and and_33 (PP31, B4, A3);
  and and_34 (PP32, B5, A2);
  and and_35 (PP33, B6, A1);
  and and_36 (PP34, B7, A0);
  and and_37 (PP20, B0, A6);
  and and_38 (PP21, B1, A5);
  and and_39 (PP22, B2, A4);
  and and_40 (PP23, B3, A3);
  and and_41 (PP24, B4, A2);
  and and_42 (PP25, B5, A1);
  and and_43 (PP26, B6, A0);
  and and_44 (PP14, B0, A5);
  and and_45 (PP15, B1, A4);
  and and_46 (PP16, B2, A3);
  and and_47 (PP17, B3, A2);
  and and_48 (PP18, B4, A1);
  and and_49 (PP19, B5, A0);
  and and_50 (PP9, B0, A4);
  and and_51 (PP10, B1, A3);
  and and_52 (PP11, B2, A2);
  and and_53 (PP12, B3, A1);
  and and_54 (PP13, B4, A0);
  and and_55 (PP5, B0, A3);
  and and_56 (PP6, B1, A2);
  and and_57 (PP7, B2, A1);
  and and_58 (PP8, B3, A0);
  and and_59 (PP2, B0, A2);
  and and_60 (PP3, B1, A1);
  and and_61 (PP4, B2, A0);
  and and_62 (PP0, B0, A1);
  and and_63 (PP1, B1, A0);
  and and_64 (LSB[0], B0, A0);

  // Other names for the same wires on the sheet: P0 = LSB[0]; P1 = LSB[1]; P2 = LSB[2]; P3 = LSB[3]; P4 = LSB[4];
  //   P5 = LSB[5]; P6 = LSB[6]; P7 = LSB[7]; P8 = MSB[0]; P9 = MSB[1]; P10 = MSB[2]; P11 = MSB[3]; P12 = MSB[4];
  //   P13 = MSB[5]; P14 = MSB[6]; P15 = MSB[7]
endmodule
