// Digital circuit NAND.dig as structural Verilog
module NAND (
  input  [7:0] A,
  input  [7:0] B,
  input  Enable,
  output [7:0] NAND
);

  wire [7:0] and_1_out, enable_1_aout, enable_1_bout;

  enable enable_1 (.Ain(A), .Enable(Enable), .Bin(B), .Aout(enable_1_aout), .Bout(enable_1_bout));
  assign and_1_out = enable_1_aout & enable_1_bout;  // And and_1, 8 bits wide
  assign NAND = ~and_1_out;  // Not not_1, 8 bits wide
endmodule
