// Digital circuit Shift_Direita.dig as structural Verilog
module Shift_Direita (
  input  Enable,
  input  [7:0] In,
  output [7:0] SD
);

  wire [0:0] enable_1_aout;

  enable enable_1 (.Ain(In), .Enable(Enable), .Bin(In), .Aout({SD[6:0], enable_1_aout[0]}));  // open: Bout

  assign SD[7] = 1'b0;
endmodule
