// Digital circuit Shift_Esquerda.dig as structural Verilog
module Shift_Esquerda (
  input  [7:0] In_8bits,
  input  Enable,
  output [7:0] SE
);

  wire [7:7] enable_1_aout;

  enable enable_1 (.Ain(In_8bits), .Enable(Enable), .Bin(In_8bits), .Aout({enable_1_aout[7], SE[7:1]}));  // open: Bout

  assign SE[0] = 1'b0;
endmodule
