// Digital circuit Somador_1bit.dig as structural Verilog
module Somador_1bit (
  input  A,
  input  B,
  input  Cin,
  output Cout,
  output Sum
);

  wire and_1_out, and_2_out, and_3_out, xor_1_out, xor_2_out;

  xor xor_1 (xor_1_out, A, B);
  and and_1 (and_1_out, A, B);
  and and_2 (and_2_out, B, Cin);
  and and_3 (and_3_out, A, Cin);
  xor xor_2 (xor_2_out, and_1_out, and_2_out);
  xor xor_3 (Sum, xor_1_out, Cin);
  xor xor_4 (Cout, xor_2_out, and_3_out);
endmodule
