// Digital circuit Somador_8bits.dig as structural Verilog
module Somador_8bits (
  input  [7:0] Ain,
  input  [7:0] Bin,
  input  Enable,
  input  Cin,
  output Cout,
  output [7:0] Sum
);

  wire somador_1bit_2_cout, somador_1bit_3_cout, somador_1bit_4_cout, somador_1bit_5_cout,
       somador_1bit_6_cout, somador_1bit_7_cout, somador_1bit_8_cout;
  wire [7:0] enable_1_aout, enable_1_bout;

  enable enable_1 (.Ain(Ain), .Enable(Enable), .Bin(Bin), .Aout(enable_1_aout), .Bout(enable_1_bout));
  Somador_1bit somador_1bit_1 (
    .A(enable_1_aout[7]), .B(enable_1_bout[7]), .Cin(somador_1bit_2_cout), .Cout(Cout), .Sum(Sum[7]));
  Somador_1bit somador_1bit_2 (
    .A(enable_1_aout[6]), .B(enable_1_bout[6]), .Cin(somador_1bit_3_cout), .Cout(somador_1bit_2_cout),
    .Sum(Sum[6]));
  Somador_1bit somador_1bit_3 (
    .A(enable_1_aout[5]), .B(enable_1_bout[5]), .Cin(somador_1bit_4_cout), .Cout(somador_1bit_3_cout),
    .Sum(Sum[5]));
  Somador_1bit somador_1bit_4 (
    .A(enable_1_aout[4]), .B(enable_1_bout[4]), .Cin(somador_1bit_5_cout), .Cout(somador_1bit_4_cout),
    .Sum(Sum[4]));
  Somador_1bit somador_1bit_5 (
    .A(enable_1_aout[3]), .B(enable_1_bout[3]), .Cin(somador_1bit_6_cout), .Cout(somador_1bit_5_cout),
    .Sum(Sum[3]));
  Somador_1bit somador_1bit_6 (
    .A(enable_1_aout[2]), .B(enable_1_bout[2]), .Cin(somador_1bit_7_cout), .Cout(somador_1bit_6_cout),
    .Sum(Sum[2]));
  Somador_1bit somador_1bit_7 (
    .A(enable_1_aout[1]), .B(enable_1_bout[1]), .Cin(somador_1bit_8_cout), .Cout(somador_1bit_7_cout),
    .Sum(Sum[1]));
  Somador_1bit somador_1bit_8 (
    .A(enable_1_aout[0]), .B(enable_1_bout[0]), .Cin(Cin), .Cout(somador_1bit_8_cout), .Sum(Sum[0]));
endmodule
