// Digital circuit Subtrador_1bit.dig as structural Verilog
module Subtrador_1bit (
  input  A,
  input  B,
  input  Bin,
  output diff,
  output Bout
);

  wire and_1_out, and_2_out, and_3_out, not_1_out, not_2_out, xor_1_out, xor_2_out;

  and and_1 (and_1_out, B, Bin);
  and and_2 (and_2_out, not_1_out, Bin);
  not not_1 (not_1_out, A);
  and and_3 (and_3_out, not_2_out, B);
  not not_2 (not_2_out, A);
  xor xor_1 (xor_1_out, A, B);
  xor xor_2 (xor_2_out, and_1_out, and_2_out);
  xor xor_3 (diff, xor_1_out, Bin);
  xor xor_4 (Bout, xor_2_out, and_3_out);
endmodule
