// Digital circuit Subtrator_8bits.dig as structural Verilog
module Subtrator_8bits (
  input  Bi,
  input  [7:0] Ain,
  input  [7:0] Bin,
  input  Enable,
  output Bout,
  output [7:0] Sub
);

  wire subtrador_1bit_2_bout, subtrador_1bit_3_bout, subtrador_1bit_4_bout, subtrador_1bit_5_bout,
       subtrador_1bit_6_bout, subtrador_1bit_7_bout, subtrador_1bit_8_bout;
  wire [7:0] enable_1_aout, enable_1_bout;

  enable enable_1 (.Ain(Ain), .Enable(Enable), .Bin(Bin), .Aout(enable_1_aout), .Bout(enable_1_bout));
  Subtrador_1bit subtrador_1bit_1 (
    .A(enable_1_aout[7]), .B(enable_1_bout[7]), .Bin(subtrador_1bit_2_bout), .diff(Sub[7]), .Bout(Bout));
  Subtrador_1bit subtrador_1bit_2 (
    .A(enable_1_aout[6]), .B(enable_1_bout[6]), .Bin(subtrador_1bit_3_bout), .diff(Sub[6]),
    .Bout(subtrador_1bit_2_bout));
  Subtrador_1bit subtrador_1bit_3 (
    .A(enable_1_aout[5]), .B(enable_1_bout[5]), .Bin(subtrador_1bit_4_bout), .diff(Sub[5]),
    .Bout(subtrador_1bit_3_bout));
  Subtrador_1bit subtrador_1bit_4 (
    .A(enable_1_aout[4]), .B(enable_1_bout[4]), .Bin(subtrador_1bit_5_bout), .diff(Sub[4]),
    .Bout(subtrador_1bit_4_bout));
  Subtrador_1bit subtrador_1bit_5 (
    .A(enable_1_aout[3]), .B(enable_1_bout[3]), .Bin(subtrador_1bit_6_bout), .diff(Sub[3]),
    .Bout(subtrador_1bit_5_bout));
  Subtrador_1bit subtrador_1bit_6 (
    .A(enable_1_aout[2]), .B(enable_1_bout[2]), .Bin(subtrador_1bit_7_bout), .diff(Sub[2]),
    .Bout(subtrador_1bit_6_bout));
  Subtrador_1bit subtrador_1bit_7 (
    .A(enable_1_aout[1]), .B(enable_1_bout[1]), .Bin(subtrador_1bit_8_bout), .diff(Sub[1]),
    .Bout(subtrador_1bit_7_bout));
  Subtrador_1bit subtrador_1bit_8 (
    .A(enable_1_aout[0]), .B(enable_1_bout[0]), .Bin(Bi), .diff(Sub[0]), .Bout(subtrador_1bit_8_bout));
  // Pins of 1 and 8 bits meet at Sub
endmodule
