// Digital circuit XOR.dig as structural Verilog
module XOR (
  input  [7:0] A,
  input  [7:0] B,
  input  Enable,
  output [7:0] XOR
);

  wire [7:0] enable_1_aout, enable_1_bout;

  enable enable_1 (.Ain(A), .Enable(Enable), .Bin(B), .Aout(enable_1_aout), .Bout(enable_1_bout));
  assign XOR = enable_1_aout ^ enable_1_bout;  // XOr xor_1, 8 bits wide
endmodule
