// Digital circuit enable.dig as structural Verilog
module enable (
  input  [7:0] Ain,
  input  Enable,
  input  [7:0] Bin,
  output [7:0] Aout,
  output [7:0] Bout
);

  and and_1 (Aout[7], Ain[7], Enable);
  and and_2 (Aout[6], Ain[6], Enable);
  and and_3 (Aout[5], Ain[5], Enable);
  and and_4 (Aout[4], Ain[4], Enable);
  and and_5 (Aout[3], Ain[3], Enable);
  and and_6 (Aout[2], Ain[2], Enable);
  and and_7 (Aout[1], Ain[1], Enable);
  and and_8 (Aout[0], Ain[0], Enable);
  and and_9 (Bout[7], Bin[7], Enable);
  and and_10 (Bout[6], Bin[6], Enable);
  and and_11 (Bout[5], Bin[5], Enable);
  and and_12 (Bout[4], Bin[4], Enable);
  and and_13 (Bout[3], Bin[3], Enable);
  and and_14 (Bout[2], Bin[2], Enable);
  and and_15 (Bout[1], Bin[1], Enable);
  and and_16 (Bout[0], Bin[0], Enable);
endmodule
