// Digital circuit seletor.dig as structural Verilog
module seletor (
  input  [2:0] IN,
  output Soma,
  output Subtracao,
  output Mult,
  output Div,
  output Shift_Direita,
  output Shift_Esquerda,
  output NAND,
  output XOR
);

  wire not_1_out, not_2_out, not_3_out;

  not not_1 (not_1_out, IN[0]);
  not not_2 (not_2_out, IN[1]);
  not not_3 (not_3_out, IN[2]);
  and and_1 (Soma, not_1_out, not_2_out, not_3_out);
  and and_2 (Subtracao, IN[0], not_2_out, not_3_out);
  and and_3 (Mult, not_1_out, IN[1], not_3_out);
  and and_4 (Div, IN[0], IN[1], not_3_out);
  and and_5 (Shift_Direita, not_1_out, not_2_out, IN[2]);
  and and_6 (Shift_Esquerda, IN[0], not_2_out, IN[2]);
  and and_7 (NAND, not_1_out, IN[1], IN[2]);
  and and_8 (XOR, IN[0], IN[1], IN[2]);
endmodule
