// Digital circuit somador_4bits.dig as structural Verilog
module somador_4bits (
  input  [3:0] B,
  input  [3:0] A,
  input  Cin,
  output [3:0] Sum,
  output [3:0] Cout
);

  wire somador_1bit_1_sum, somador_1bit_2_sum, somador_1bit_3_sum;

  Somador_1bit somador_1bit_1 (.A(A[0]), .B(B[0]), .Cin(Cin), .Cout(Sum[0]), .Sum(somador_1bit_1_sum));
  Somador_1bit somador_1bit_2 (.A(A[1]), .B(B[1]), .Cin(somador_1bit_1_sum), .Cout(Sum[1]), .Sum(somador_1bit_2_sum));
  Somador_1bit somador_1bit_3 (.A(A[2]), .B(B[2]), .Cin(somador_1bit_2_sum), .Cout(Sum[2]), .Sum(somador_1bit_3_sum));
  // Somador_1bit somador_1bit_4: pin names not known; wires that end beside it: A[3], B[3], somador_1bit_3_sum, Sum[3], Cout
endmodule
